# Fritzing sketch SmartLightHubNode_schematic (saved by Fritzing 0.9.2b)
breadboards: 1

parts:
  Bauteil1 = Arduino Mega 2560 (Rev3)
  Bauteil2 = Logic Level Converter
  U1 = LMZ14203 [package=to-pmod-7]
  R1 = Resistor [tolerance=±5% resistance=100k package="0402 [SMD]"]
  C1 = Electrolytic Capacitor [capacitance=0.22mF voltage=20V package="0405 [SMD, electrolytic]"]
  R2 = Resistor [tolerance=±5% resistance=107k package="0402 [SMD]"]
  R3 = Resistor [tolerance=±5% resistance=107k package="0402 [SMD]"]
  C2 = Electrolytic Capacitor [capacitance=0.22mF voltage=20V package="0405 [SMD, electrolytic]"]
  C3 = Electrolytic Capacitor [capacitance=100µF package="200 mil [THT, electrolytic]"]
  U2 = MAX485 [package=dil08]
  R4 = Resistor [tolerance=±5% resistance=100k package="0402 [SMD]"]
  XLR1 = XLR3_NCFAH2 [package=xlr3_nc3fah2]
  JP1 = Header 6 [package=1x06-smd]
  Raspberry_Pi1 = Raspberry Pi 2

nets:
  N1: Bauteil1.D19/RX1, Bauteil2.RX_HV
  N2: Bauteil1.D18/TX1, Bauteil2.TX_HV
  5V: Bauteil1.5V, Bauteil2.HV, U1.VOUT, R3.Pin_1, C2.+, C3.+, U2.VCC, Raspberry_Pi1.5V
  GND: Bauteil1.GND, Bauteil2.GND, U1.EN, C1.-, R2.Pin_1, C3.-, U2.RO, U2.GND, R4.Pin_0, XLR1.1, XLR1.G, Raspberry_Pi1.GND
  VIN: Bauteil1.VIN, U1.VIN, R1.Pin_1
  N3: Bauteil1.D0_RX0, U2.DI
  N4: Bauteil1.D23, JP1.1
  N5: Bauteil1.D25, JP1.2
  N6: Bauteil1.D27, JP1.3
  N7: Bauteil1.D29, JP1.4
  N8: Bauteil1.D31, JP1.5
  N9: Bauteil1.D33, JP1.6
  N10: Bauteil2.RX_LV, Raspberry_Pi1.GPIO14
  N11: Bauteil2.TX_LV, Raspberry_Pi1.GPIO15
  N12: U1.RON, R1.Pin_0
  N13: U1.SS, C1.+
  N14: U1.FB, R2.Pin_0, R3.Pin_0, C2.-
  N15: U2.RE, R4.Pin_1
  N16: U2.A, XLR1.3
  N17: U2.B, XLR1.2

notes:
  Relais-Ouput
  DMX-Output
  Power-In 7-42 V
